# Fritzing sketch Schematic_fritzing (saved by Fritzing 0.9.10b)
breadboards: 1

parts:
  Arduino_NANO = Arduino Nano (Rev3.0)
  C1_2000uF = Capacitor Polarized [package=cpol-radial-10uf-25v]
  C2_470uF = Capacitor Polarized [package=cpol-radial-10uf-25v]
  D1 = Rectifier Diode [package="Melf DO-213 AA [SMD]"]
  U1 = POT [knob_status=50% power=0.5W package=pot_mammoth]
  M1_FAN = DC Motor [voltage_(max)=6V voltage_(min)=3V]

nets:
  0V PSU/Antenna2/GND/LED -: Arduino_NANO.GND, C1_2000uF.-, C2_470uF.-, M1_FAN.pin_2
  LED_DATA: Arduino_NANO.D2
  5V from USB: Arduino_NANO.5V, C2_470uF.+, D1.cathode
  Antenna1: Arduino_NANO.A0
  5V PSU/LED +: C1_2000uF.+, D1.anode, U1.E
  N1: U1.S, M1_FAN.pin_1
